# Fritzing sketch Pinball (saved by Fritzing 0.9.3b)
breadboards: 2

parts:
  LCD1 = LCD screen
  LED1 = smd LED [color="Blue (525nm)" package="0603 [SMD]"]  # not connected
  LED2 = smd LED [color="Green (570nm)" package="0603 [SMD]"]
  LED4 = smd LED [color="Red (633nm)" package="0603 [SMD]"]
  R1 = Resistor [tolerance=±5% resistance=150 package="0402 [SMD]"]
  R2 = Resistor [tolerance=±5% resistance=150 package="0402 [SMD]"]
  R3 = Resistor [tolerance=±5% resistance=150 package="0402 [SMD]"]
  R4 = Resistor [tolerance=±5% resistance=150 package="0402 [SMD]"]
  R5 = Rotary Potentiometer (Large) [maximum_resistance=10kΩ package=THT]
  R6 = Resistor [tolerance=±5% resistance=150 package=THT]
  R7 = Resistor [tolerance=±20% resistance=150 package=THT]
  LED5 = LED - 5mm [color="Green (570nm)" package="5 mm [THT]"]
  LED6 = LED - 5mm [color="Blue (525nm)" package="5 mm [THT]"]
  BAT1 = BC9VPC [package=bc9vpc]
  Componente1 = Arduino Uno (Rev3)
  LED3 = smd LED [color="Yellow (595nm)" package="0805 [SMD]"]
  S2 = Pushbutton [package=THT]
  TCRT1 = TCRT5000 sensor module [part_number=151608]  # not connected
  TCRT2 = TCRT5000 sensor module [part_number=151608]  # not connected
  TCRT3 = TCRT5000 sensor module [part_number=151608]  # not connected
  TCRT4 = TCRT5000 sensor module [part_number=151608]  # not connected
  TCRT5 = TCRT5000 sensor module [part_number=151608]  # not connected
  TCRT6 = TCRT5000 sensor module [part_number=151608]  # not connected
  R8 = Resistor [tolerance=±5% resistance=330 package=THT]
  R9 = Resistor [tolerance=±5% resistance=330 package=THT]
  R10 = Resistor [tolerance=±5% resistance=330 package=THT]
  R11 = Resistor [tolerance=±5% resistance=330 package=THT]
  R12 = Resistor [tolerance=±5% resistance=330 package=THT]
  R13 = Resistor [tolerance=±5% resistance=330 package=THT]
  R14 = Resistor [tolerance=±5% resistance=10k package=THT]
  R16 = Resistor [tolerance=±5% resistance=10k package=THT]
  R17 = Resistor [tolerance=±5% resistance=10k package=THT]
  R18 = Resistor [tolerance=±5% resistance=10k package=THT]
  R19 = Resistor [tolerance=±5% resistance=10k package=THT]
  R20 = Resistor [tolerance=±5% resistance=10k package=THT]

nets:
  VSS: LCD1.VSS, LCD1.R/W, LCD1.LED-, LED2.cathode, LED2.anode, LED4.cathode, LED4.anode, R1.Pin_1, R2.Pin_1, R3.Pin_1, R4.Pin_1, R5.leg2, R6.Pin_1, R7.Pin_1, LED5.cathode, LED5.anode, LED6.cathode, LED6.anode, BAT1.V-, Componente1.GND, LED3.cathode, LED3.anode
  VDD: LCD1.VDD, LCD1.LED+, R5.leg1, Componente1.5V, R8.Pin_1, R9.Pin_1, R10.Pin_1, R11.Pin_1, R12.Pin_1, R13.Pin_1
  N1: LCD1.V0, R5.wiper
  N2: LCD1.RS, Componente1.D6_PWM
  N3: LCD1.E, Componente1.D7
  N4: LCD1.DB4, Componente1.D5_PWM
  N5: LCD1.DB5, Componente1.D4
  N6: LCD1.DB6, Componente1.D3_PWM
  N7: LCD1.DB7, Componente1.D2
  N8: R1.Pin_0, Componente1.D13/SCK
  N9: R2.Pin_0, Componente1.D12/MISO
  N10: R3.Pin_0, Componente1.D11_PWM/MOSI
  N11: R4.Pin_0, Componente1.D10_PWM/SS
  N12: R6.Pin_0, Componente1.D8
  N13: R7.Pin_0, Componente1.D9_PWM
  N14: BAT1.V+, S2.leg1
  N15: Componente1.A0, R14.Pin_1
  N16: Componente1.A1, R20.Pin_1
  N17: Componente1.A2, R19.Pin_1
  N18: Componente1.A3, R18.Pin_1
  N19: Componente1.A4/SDA, R17.Pin_1
  N20: Componente1.A5/SCL, R16.Pin_1
  N21: Componente1.VIN, S2.leg0

custom parts:
  TCRT5000 sensor module: breakout board with TCRT5000

// code stored in the sketch: Pinball.ino
//Bibliotecas
#include <LiquidCrystal.h>

//Definindo os pinos que serão utilizados para ligação ao display LCD
LiquidCrystal lcd(12, 11, 5, 4, 3, 2);

//Definindo pinos dos LED
int pinoLed_1 = 8; //Pino digital utilizado pelo LED 1 - Verde
int pinoLed_2 = 9; //Pino digital utilizado pelo LED 2 - Azul
int pinoLed_3 = 10; //Pino digital utilizado pelo LED 3 - Amarelo
int pinoLed_4 = 13; //Pino digital utilizado pelo LED 4 - Vermelho
int pinoLed_5 = 16; //Pino analogico A2 transformado em pino digital utilizado pelo LED 5 - Verde
int pinoLed_6 = 17; //Pino analogico A3 transformado em pino digital utilizado pelo LED 6 - Azul

// Cores LED e Pontos
// Verde = LED 1 e 5 = 1 ponto
// Azul = LED 2 e 6 = 2 ponto
// Amarelo = LED 3 = 3 ponto
// Vermelho = LED 4 = 0 ponto

//Definindo pinos dos sensores óptico tcrt5000
int pinoSensor_1 = 7; //Pino digital utilizado pelo sensor 1
int pinoSensor_2 = 6; //Pino digital utilizado pelo sensor 2
int pinoSensor_3 = 14; //Pino analogico A0 transformado em pino digital utilizado pelo sensor 3
int pinoSensor_4 = 15; //Pino analogico A1 transformado em pino digital utilizado pelo sensor 4
int pinoSensor_5 = 18; //Pino analogico A4 transformado em pino digital utilizado pelo sensor 5
int pinoSensor_6 = 19; //Pino analogico A5 transformado em pino digital utilizado pelo sensor 6

// Relação entre LED e sensores - Pinos
// pinoSensor_1 -> pinoLed_1 - Pinos 7 e 8
// pinoSensor_2 -> pinoLed_2 - Pinos 6 e 9
// pinoSensor_3 -> pinoLed_3 - Pinos A0 e 10
// pinoSensor_4 -> pinoLed_4 - Pinos A1 e 13
// pinoSensor_5 -> pinoLed_5 - Pinos A4 e A2
// pinoSensor_6 -> pinoLed_6 - Pinos A5 e A3

// Variáveis
int point = 0; //Contador de pontos
int stop = 500; //Tempo de parada para o delay

void setup() {
  //Define o número de colunas e linhas do LCD
  lcd.begin(16, 2);
  
  // Inicializando os Sensores
  pinMode(pinoSensor_1, INPUT); //Definindo o pino como entrada para o sensor 1
  pinMode(pinoSensor_2, INPUT); //Definindo o pino como entrada para o sensor 2
  pinMode(pinoSensor_3, INPUT); //Definindo o pino como entrada para o sensor 3
  pinMode(pinoSensor_4, INPUT); //Definindo o pino como entrada para o sensor 4
  pinMode(pinoSensor_5, INPUT); //Definindo o pino como entrada para o sensor 5
  pinMode(pinoSensor_6, INPUT); //Definindo o pino como entrada para o sensor 6

  // Inicializando os LED
  pinMode(pinoLed_1, OUTPUT); //Definindo o pino como saída para o LED 1 - Verde
  pinMode(pinoLed_2, OUTPUT); //Definindo o pino como saída para o LED 2 - Azul
  pinMode(pinoLed_3, OUTPUT); //Definindo o pino como saída para o LED 3 - Amarelo
  pinMode(pinoLed_4, OUTPUT); //Definindo o pino como saída para o LED 4 - Vermelho
  pinMode(pinoLed_5, OUTPUT); //Definindo o pino como saída para o LED 5 - Verde
  pinMode(pinoLed_6, OUTPUT); //Definindo o pino como saída para o LED 6 - Azul
  
  // Desligando os LED
  digitalWrite(pinoLed_1, LOW); //LED 1 inicia desligado
  digitalWrite(pinoLed_2, LOW); //LED 2 inicia desligado
  digitalWrite(pinoLed_3, LOW); //LED 3 inicia desligado
  digitalWrite(pinoLed_4, LOW); //LED 4 inicia desligado
  digitalWrite(pinoLed_5, LOW); //LED 5 inicia desligado
  digitalWrite(pinoLed_6, LOW); //LED 6 inicia desligado
}

void loop() {
  //Sensor
  if ((digitalRead(pinoSensor_1) == LOW) || (digitalRead(pinoSensor_5) == LOW)){ //Se a leitura do sensor 1 ou 5 (Verde) for igual a LOW, faz
    digitalWrite(pinoLed_1, HIGH); //Acende o LED 1 - Verde
    point=point+1; //Adiciona 1 ponto
  }else if((digitalRead(pinoSensor_2) == LOW) || (digitalRead(pinoSensor_6) == LOW)){ //Se a leitura do sensor 2 ou 6 (Azul) for igual a LOW, faz
		digitalWrite(pinoLed_2, HIGH); //Acende o LED 2 - Azul
    point=point+2; //Adiciona 2 ponto
  }else if(digitalRead(pinoSensor_3) == LOW){ //Se a leitura do sensor 3 (Amarelo) for igual a LOW, faz
		digitalWrite(pinoLed_3, HIGH); //Acende o LED 3 - Amarelo
    point=point+3; //Adiciona 3 ponto
  }else if(digitalRead(pinoSensor_4) == LOW){ //Se a leitura do sensor 4 (Vermelho) for igual a LOW, faz
		digitalWrite(pinoLed_4, HIGH); //Acende o LED 4 - Vermelho
    point=0; //Reinicia a contagem
  }
  
  //LCD
  //Limpa a tela
  lcd.clear();
  //Posiciona o cursor na coluna 1, linha 0;
  lcd.setCursor(1, 0);
  //Envia o texto entre aspas para o LCD
  lcd.print("Jogo Placar");
  //Posiciona o cursor na coluna 1, linha 1;
  lcd.setCursor(1, 1);
  //Imprime Contador de pontuação
  lcd.print(point);
  delay(stop);
  
  // Apagar LED
  digitalWrite(pinoLed_1, LOW); //Apaga o LED 1
  digitalWrite(pinoLed_2, LOW); //Apaga o LED 2
  digitalWrite(pinoLed_3, LOW); //Apaga o LED 3
  digitalWrite(pinoLed_4, LOW); //Apaga o LED 4
  digitalWrite(pinoLed_5, LOW); //Apaga o LED 5
  digitalWrite(pinoLed_6, LOW); //Apaga o LED 6
}
